# Fritzing sketch all-together (saved by Fritzing 0.9.4)
breadboards: 1

parts:
  Part1 = Arduino Uno (Rev3) - ICSP
  ZS-042_RTC1 = ZS-042 RTC Module
  Part2 = US-100 Ultrasonic Rangefinder
  U1 = ESP8266 WiFi Module [part_number=ESP8266]
  Mod1 = Lipo Battery Pack
  Part3 = Solar Cell
  D1 = Rectifier Diode [package="Melf DO-213 AA [SMD]"]

nets:
  N1: Part1.A4/SDA, ZS-042_RTC1.SDA
  N2: Part1.A5/SCL, ZS-042_RTC1.SCL
  N3: Part1.D2, ZS-042_RTC1.SQW
  N4: Part1.D4, Part2.Trig/Tx
  N5: Part1.D5_PWM, Part2.Echo/Rx
  N6: Part1.D6_PWM, U1.TXD
  N7: Part1.D7, U1.RXD
  VCC: Part1.3V3, ZS-042_RTC1.VCC, Part2.VCC, U1.VCC, U1.CH_PD, Mod1.3.3V
  GND: Part1.GND, ZS-042_RTC1.GND, Part2.GND, Part2.GND*, U1.GND, Mod1.GND
  N8: Mod1.?1, Part3.-
  N9: Mod1.?2, D1.cathode
  N10: Part3.+, D1.anode

custom parts:
  ESP8266 WiFi Module: Generic WiFi Module based on the ESP8266 with onboard PCB antenna and UART communications
  Lipo Battery Pack: Micro USB 5V 16340 18650 lithium Battery Shield V3 Wemos ESP32 ESP8266 Module
