# Fritzing sketch all-together-mini (saved by Fritzing 0.9.4)
breadboards: 1

parts:
  ZS-042_RTC1 = ZS-042 RTC Module
  Part2 = US-100 Ultrasonic Rangefinder
  U1 = ESP8266 WiFi Module [part_number=ESP8266]
  Mod1 = Lipo Battery Pack
  Part3 = Solar Cell
  D1 = Rectifier Diode [package="Melf DO-213 AA [SMD]"]
  Part4 = Arduino Pro Mini (3.3V)

nets:
  GND: ZS-042_RTC1.GND, Part2.GND, Part2.GND*, U1.GND, Mod1.GND, Part4.GND
  VCC: ZS-042_RTC1.VCC, Part2.VCC, U1.VCC, U1.CH_PD, Mod1.3.3V, Part4.VCC
  N1: ZS-042_RTC1.SDA, Part4.A4
  N2: ZS-042_RTC1.SCL, Part4.A5
  N3: ZS-042_RTC1.SQW, Part4.D2
  N4: Part2.Trig/Tx, Part4.D6
  N5: Part2.Echo/Rx, Part4.D7
  N6: U1.RXD, Part4.D9
  N7: U1.TXD, Part4.D8
  N8: Mod1.?1, Part3.-
  N9: Mod1.?2, D1.cathode
  N10: Part3.+, D1.anode

custom parts:
  ESP8266 WiFi Module: Generic WiFi Module based on the ESP8266 with onboard PCB antenna and UART communications
  Lipo Battery Pack: Micro USB 5V 16340 18650 lithium Battery Shield V3 Wemos ESP32 ESP8266 Module
