# Fritzing sketch sleep-mk2 (saved by Fritzing 0.9.4)
breadboards: 1

parts:
  Part1 = Arduino Uno (Rev3) - ICSP
  ZS-042_RTC1 = ZS-042 RTC Module

nets:
  N1: Part1.A4/SDA, ZS-042_RTC1.SDA
  N2: Part1.A5/SCL, ZS-042_RTC1.SCL
  N3: Part1.D2, ZS-042_RTC1.SQW
  3V3: Part1.3V3, ZS-042_RTC1.VCC
  GND: Part1.GND, ZS-042_RTC1.GND
